# Fritzing sketch TB6612 con arduinoUNO (saved by Fritzing 0.9.3b)

parts:
  M1 = DC Motor
  M2 = DC Motor
  Componente1 = Arduino Uno (Rev3)
  VCC1 = Battery block 9V  # not connected
  TB6612 = Motor Driver 1A Dual TB6612FNG

nets:
  N1: M1.pin_1, TB6612.A02
  N2: M1.pin_2, TB6612.A01
  N3: M2.pin_1, TB6612.B02
  N4: M2.pin_2, TB6612.B01
  N5: Componente1.D8, TB6612.BIN2
  GND: Componente1.GND, TB6612.GND
  N6: Componente1.D2, TB6612.AIN1
  N7: Componente1.D3_PWM, TB6612.STBY
  N8: Componente1.D4, TB6612.AIN2
  N9: Componente1.D5_PWM, TB6612.PWMB
  N10: Componente1.D6_PWM, TB6612.PWMA
  N11: Componente1.D7, TB6612.BIN1
  5V: Componente1.5V, TB6612.VCC
  N12: Componente1.VIN, TB6612.VM

notes:
  CTR_R_1 (In 1)
  CTR_R_2 (In 2)
  PWM_R  (Enable 1)
  CTR_R_1 (In 3)
  CTR_R_2 (In 4)
  PWM_L  (Enable 2)
  Para manejar los motores es necesario que Enable este a +5V
  en setup:
  pinMode (3, OUTPUT);
  digitalWrite (3, HIGH);

// code stored in the sketch: Untitled4.ino
#include <RobotMovil.h>

RobotMovil robot;

void setup()
{
}

void loop()
{
  robot.forward(255,255,1000); // avance con velocidad rueda derecha, rueda izquierda y tiempo en ms
  robot.reverse(0,120,2000); // idem pero retroceso
  robot.rotate(1000); // giro durante un tiempo en ms, valores negativo o positivos indican sentido de giro
  robot.rotate(-1000); // giro durante un tiempo en ms, valores negativo o positivos indican sentido de giro
  robot.brake(1000); // detiene el robot un tiempo
}
