# Fritzing sketch L293D con arduinoUNO (saved by Fritzing 0.9.3b)
breadboards: 1

parts:
  M1 = DC Motor
  M2 = DC Motor
  IC1 = L293D [package=THT]
  Componente1 = Arduino Uno (Rev3)
  VCC1 = Battery block 9V

nets:
  N1: M1.pin_1, IC1.Out_2_(_Controlled_by_Enable_1_)
  N2: M1.pin_2, IC1.Out_1_(_Controlled_by_Enable_1_)
  N3: M2.pin_1, IC1.Out_3_(_Controlled_by_Enable_2_)
  N4: M2.pin_2, IC1.Out_4_(_Controlled_by_Enable_2_)
  N5: IC1.Enable_1, Componente1.D6_PWM
  N6: IC1.In_1, Componente1.D2
  N7: IC1.0V, Componente1.GND, VCC1.-
  N8: IC1.In_2, Componente1.D4
  N9: IC1.+Vmotor, Componente1.VIN, VCC1.+
  N10: IC1.Enable_2, Componente1.D5_PWM
  N11: IC1.In_3, Componente1.D7
  N12: IC1.In_4, Componente1.D8
  N13: IC1.+V, Componente1.5V

notes:
  CTR_R_1 (In 1)
  CTR_R_2 (In 2)
  PWM_R  (Enable 1)
  CTR_R_1 (In 3)
  CTR_R_2 (In 4)
  PWM_L  (Enable 2)

// code stored in the sketch: Untitled4.ino
#include <RobotMovil.h>

RobotMovil robot;

void setup()
{
}

void loop()
{
  robot.forward(255,255,1000); // avance con velocidad rueda derecha, rueda izquierda y tiempo en ms
  robot.reverse(0,120,2000); // idem pero retroceso
  robot.rotate(1000); // giro durante un tiempo en ms, valores negativo o positivos indican sentido de giro
  robot.rotate(-1000); // giro durante un tiempo en ms, valores negativo o positivos indican sentido de giro
  robot.brake(1000); // detiene el robot un tiempo
}
